// Logisim project cricuit.circ as structural Verilog: 14 circuits, main circuit main
module main (
);

  wire clock_1_out, pd_mine_1_f7, pd_mine_1_zero, uc_1_out_6, uc_1_out_9, uc_1_out_10, uc_1_out_11;
  wire [1:0] uc_1_out_7, uc_1_out_8, uc_1_out_12;
  wire [2:0] pd_mine_1_f3, uc_1_out_5;
  wire [6:0] pd_mine_1_op;
  wire [15:0] pd_mine_1_pc;
  wire [31:0] memory_1_out_6, memory_1_out_7, pd_mine_1_out_16, pd_mine_1_out_18;

  Clock clock_1 (.out(clock_1_out));
  UC uc_1 (
    .in_1(pd_mine_1_op), .in_2(pd_mine_1_f7), .in_3(pd_mine_1_f3), .out_5(uc_1_out_5), .out_6(uc_1_out_6),
    .out_7(uc_1_out_7), .out_8(uc_1_out_8), .out_9(uc_1_out_9), .out_10(uc_1_out_10), .out_11(uc_1_out_11),
    .out_12(uc_1_out_12), .in_4(pd_mine_1_zero));
  pd_mine pd_mine_1 (
    .inmSrc(uc_1_out_12), .resSrc(uc_1_out_8), .pc(pd_mine_1_pc), .f7(pd_mine_1_f7), .f3(pd_mine_1_f3),
    .op(pd_mine_1_op), .out_18(pd_mine_1_out_18), .zero(pd_mine_1_zero), .out_16(pd_mine_1_out_16),
    .branch(uc_1_out_6), .jump(uc_1_out_7), .clk(clock_1_out), .en(uc_1_out_11), .aluSrc(uc_1_out_10),
    .aluControl(uc_1_out_5), .in_10(memory_1_out_7), .in_13(memory_1_out_6));  // open: op_m, csr_read_sel, in_12, csr_data_s
  Memory memory_1 (
    .in_1(clock_1_out), .in_2(uc_1_out_9), .in_3(pd_mine_1_out_16[15:0]), .in_4(pd_mine_1_out_18),
    .in_5(pd_mine_1_pc), .out_6(memory_1_out_6), .out_7(memory_1_out_7));
endmodule

module pc (
  input  in_1,
  input  [15:0] in_2,
  output [15:0] out_3
);
endmodule

module SE (
  input  [31:0] in_1,
  input  [1:0] in_2,
  output [31:0] out_3
);
endmodule

module BR (
  input  in_1,
  input  [4:0] in_2,
  input  [4:0] in_3,
  input  [4:0] in_4,
  input  [31:0] in_5,
  input  in_6,
  output [31:0] out_7,
  output [31:0] out_8
);
endmodule

module ALU (
  input  [31:0] in_1,
  input  [31:0] in_2,
  input  [2:0] in_3,
  output [31:0] out_4,
  output out_5
);
endmodule

module pd_mine (
  input  [2:0] aluControl,
  input  [1:0] inmSrc,
  input  aluSrc,
  input  op_m,
  input  branch,
  input  [1:0] jump,
  input  clk,
  input  en,
  input  csr_read_sel,
  input  [31:0] in_10,
  input  [1:0] resSrc,
  input  in_12,
  input  [31:0] in_13,
  input  csr_data_s,
  output zero,
  output [31:0] out_16,
  output [15:0] pc,
  output [31:0] out_18,
  output [6:0] op,
  output [2:0] f3,
  output f7
);

  wire [15:0] multiplexer_1_out;
  wire [31:0] adder_1_out, adder_2_out, bit_extender_1_out, bit_extender_2_out, br_1_out_7, csr_1_out_5,
       multiplexer_2_out, multiplexer_3_out, multiplexer_4_out, multiplexer_5_out, multiplexer_6_out,
       multiplexer_7_out, se_1_out_3, undriven;

  Multiplexer #(.width(16), .enable("false")) multiplexer_1 (
    .in0(pc), .in1(csr_1_out_5[15:0]), .out(multiplexer_1_out), .sel(op_m));
  Multiplexer #(.width(32), .enable("false")) multiplexer_2 (
    .in0(32'h4), .in1(se_1_out_3), .out(multiplexer_2_out), .sel(branch));
  assign bit_extender_1_out = {{16{1'b0}}, multiplexer_1_out};  // Bit_Extender bit_extender_1
  assign bit_extender_2_out = {{16{1'b0}}, pc};  // Bit_Extender bit_extender_2
  Adder #(.width(32)) adder_1 (.a(multiplexer_2_out), .b(bit_extender_1_out), .out(adder_1_out));  // open: cin, cout
  Adder #(.width(32)) adder_2 (.a(bit_extender_2_out), .b(se_1_out_3), .out(adder_2_out));  // open: cin, cout
  Multiplexer #(.select(2), .width(32), .enable("false")) multiplexer_3 (
    .in0({32{1'b0}}), .in1(adder_1_out), .in2(adder_2_out), .out(multiplexer_3_out), .sel(jump));  // open: in3
  pc pc_1 (.in_1(clk), .in_2(multiplexer_3_out[15:0]), .out_3(pc));
  SE se_1 (.in_1(undriven), .in_2(inmSrc), .out_3(se_1_out_3));
  Multiplexer #(.width(32), .enable("false")) multiplexer_4 (
    .in0(in_13), .in1(csr_1_out_5), .out(multiplexer_4_out), .sel(csr_read_sel));
  Multiplexer #(.width(32), .enable("false")) multiplexer_5 (
    .in0(br_1_out_7), .in1(se_1_out_3), .out(multiplexer_5_out), .sel(csr_data_s));
  Multiplexer #(.select(2), .width(32), .enable("false")) multiplexer_6 (
    .in0(out_16), .in1(multiplexer_4_out), .in2(se_1_out_3), .in3(adder_1_out), .out(multiplexer_6_out),
    .sel(resSrc));
  CSR csr_1 (.in_1(clk), .in_2(in_12), .in_3(in_10[31:20]), .in_4(multiplexer_5_out), .out_5(csr_1_out_5));
  BR br_1 (
    .in_1(clk), .in_2(undriven[19:15]), .in_3(undriven[24:20]), .in_4(undriven[11:7]),
    .in_5(multiplexer_6_out), .in_6(en), .out_7(br_1_out_7), .out_8(out_18));
  Multiplexer #(.width(32), .enable("false")) multiplexer_7 (
    .in0(out_18), .in1(se_1_out_3), .out(multiplexer_7_out), .sel(aluSrc));
  ALU alu_1 (.in_1(br_1_out_7), .in_2(multiplexer_7_out), .in_3(aluControl), .out_4(out_16), .out_5(zero));

  assign f3 = in_10[14:12];
  assign f7 = in_10[30];
  assign op = in_10[6:0];

  // Notes on the sheet:
  //   s_pc
  //   s_inmExt
  //   add1
  //   m4
  //   readData
  //   m1
  //   instr
  //   m3
  //   s_inmExt
  //   s_alu_res
  //   m2
  //   writeData
  //   aluRes
endmodule

module DM (
  input  in_1,
  input  in_2,
  input  [15:0] in_3,
  input  [31:0] in_4,
  output [31:0] out_5
);
endmodule

module IM (
  input  [15:0] in_1,
  output [31:0] out_2
);
endmodule

module Memory (
  input  in_1,
  input  in_2,
  input  [15:0] in_3,
  input  [31:0] in_4,
  input  [15:0] in_5,
  output [31:0] out_6,
  output [31:0] out_7
);

  DM dm_1 (.in_1(in_1), .in_2(in_2), .in_3(in_3), .in_4(in_4), .out_5(out_6));
  IM im_1 (.in_1(in_5), .out_2(out_7));
endmodule

module mainDeco (
  input  [6:0] in_1,
  output branch,
  output [1:0] jump,
  output [1:0] resSrc,
  output memWrite,
  output aluSrc,
  output [1:0] inmSrc,
  output regWrite,
  output [1:0] aluOp
);
endmodule

module ALUDeco (
  input  in_1,
  input  in_2,
  input  [2:0] in_3,
  input  [1:0] in_4,
  output [2:0] out_5
);
endmodule

module UC (
  input  [6:0] in_1,
  input  in_2,
  input  [2:0] in_3,
  input  in_4,
  output [2:0] out_5,
  output out_6,
  output [1:0] out_7,
  output [1:0] out_8,
  output out_9,
  output out_10,
  output out_11,
  output [1:0] out_12
);

  wire [1:0] maindeco_1_aluop;

  ALUDeco aludeco_1 (.in_1(in_1[5]), .in_2(in_2), .in_3(in_3), .in_4(maindeco_1_aluop), .out_5(out_5));
  mainDeco maindeco_1 (
    .in_1(in_1), .branch(out_6), .jump(out_7), .resSrc(out_8), .memWrite(out_9), .aluSrc(out_10),
    .inmSrc(out_12), .regWrite(out_11), .aluOp(maindeco_1_aluop));
endmodule

module iReg (
  input  in_1,
  input  [15:0] in_2,
  output [15:0] out_3
);
endmodule

module CSR (
  input  in_1,
  input  in_2,
  input  [11:0] in_3,
  input  [31:0] in_4,
  output [31:0] out_5
);
endmodule
